// Logisim project BasicComputer.circ as structural Verilog: 1 circuit, main circuit CompleteComputer
module CompleteComputer (
  input  [3:0] in_1
);

  wire control_unit_1_p2, control_unit_1_p4, control_unit_1_p6, control_unit_1_p8, control_unit_1_p9,
       control_unit_1_p10, control_unit_1_p11, control_unit_1_p12, control_unit_1_p13, control_unit_1_p14,
       control_unit_1_p15, control_unit_1_p16, control_unit_1_p17, control_unit_1_p18, control_unit_1_p19,
       control_unit_1_p20, control_unit_1_p21, control_unit_1_p22, control_unit_1_p23, control_unit_1_p24,
       control_unit_1_p25, control_unit_1_p26, control_unit_1_p27, control_unit_1_p28, control_unit_1_p29,
       control_unit_1_p30, CP_out, Reset_out;
  wire [3:0] AC_a, AC_a_2, AC_a_3, AC_a_4, control_unit_1_p1, control_unit_1_p1_2, control_unit_1_p1_3,
       control_unit_1_p1_4, controlled_buffer_1_out, controlled_buffer_1_out_2, controlled_buffer_1_out_3,
       controlled_buffer_3_out, DR_a, DR_a_2, DR_a_3, DR_a_4, SC_a0;
  wire [7:0] INPR_a, OUTR_a;
  wire [11:0] AR_a, PC_a;
  wire [15:0] bit16_alsu_1_f, ram_1_dout, TR_a;

  Clock CP (.out(CP_out));
  Button Reset (.out(Reset_out));
  Bit4_Counter SC (
    .INR(1'b1), .CP(CP_out), .CLR(Reset_out), .A0(SC_a0[0]), .A1(SC_a0[1]), .A2(SC_a0[2]), .A3(SC_a0[3]));
  Hex_Digit_Display hex_digit_display_1 (.value(SC_a0));  // open: dp
  // Control_Unit control_unit_1: pin names not known; wires that end beside it: {control_unit_1_p1_4, control_unit_1_p1_3, control_unit_1_p1_2, control_unit_1_p1}, control_unit_1_p2, 1'b0, control_unit_1_p4, SC_a0, control_unit_1_p6, Reset_out, control_unit_1_p8, control_unit_1_p9, control_unit_1_p10, control_unit_1_p11, control_unit_1_p12, control_unit_1_p13, control_unit_1_p14, control_unit_1_p15, control_unit_1_p16, control_unit_1_p17, control_unit_1_p18, control_unit_1_p19, control_unit_1_p20, control_unit_1_p21, control_unit_1_p22, control_unit_1_p23, control_unit_1_p24, control_unit_1_p25, control_unit_1_p26, control_unit_1_p27, control_unit_1_p28, control_unit_1_p29, control_unit_1_p30
  Bit16_ALSU bit16_alsu_1 (
    .A({AC_a_4, AC_a_3, AC_a_2, AC_a}), .B({DR_a_4, DR_a_3, DR_a_2, DR_a}), .S(in_1), .F(bit16_alsu_1_f));  // open: C_prev, C_next
  RAM #(.addrWidth(12), .dataWidth(16)) ram_1 (
    .addr(AR_a), .we(control_unit_1_p17), .oe(control_unit_1_p16), .clk(CP_out),
    .din({controlled_buffer_3_out, controlled_buffer_1_out_3, controlled_buffer_1_out_2, controlled_buffer_1_out}),
    .dout(ram_1_dout));
  Bit12_Register AR (
    .I({controlled_buffer_1_out_3, controlled_buffer_1_out_2, controlled_buffer_1_out}),
    .Load(control_unit_1_p8), .INR(control_unit_1_p9), .CLR(control_unit_1_p10), .CP(CP_out), .A(AR_a));  // open: C
  Bit12_Register PC (
    .I({controlled_buffer_1_out_3, controlled_buffer_1_out_2, controlled_buffer_1_out}),
    .Load(control_unit_1_p18), .INR(control_unit_1_p19), .CLR(control_unit_1_p20), .CP(CP_out), .A(PC_a));  // open: C
  Bit16_Register DR (
    .I({controlled_buffer_3_out, controlled_buffer_1_out_3, controlled_buffer_1_out_2, controlled_buffer_1_out}),
    .Load(control_unit_1_p11), .INR(control_unit_1_p12), .CLR(control_unit_1_p13), .CP(CP_out),
    .A({DR_a_4, DR_a_3, DR_a_2, DR_a}));  // open: C
  Bit16_Register AC (
    .I(bit16_alsu_1_f), .Load(control_unit_1_p2), .INR(control_unit_1_p4), .CLR(control_unit_1_p6),
    .CP(CP_out), .A({AC_a_4, AC_a_3, AC_a_2, AC_a}));  // open: C
  Bit8_Register INPR (.CLR(Reset_out), .CP(CP_out), .A(INPR_a));  // open: I, Load, INR, C
  Bit16_Register IR (
    .I({controlled_buffer_3_out, controlled_buffer_1_out_3, controlled_buffer_1_out_2, controlled_buffer_1_out}),
    .Load(control_unit_1_p14), .INR(1'b0), .CLR(control_unit_1_p15), .CP(CP_out),
    .A({control_unit_1_p1_4, control_unit_1_p1_3, control_unit_1_p1_2, control_unit_1_p1}));  // open: C
  Bit16_Register TR (
    .I({controlled_buffer_3_out, controlled_buffer_1_out_3, controlled_buffer_1_out_2, controlled_buffer_1_out}),
    .Load(control_unit_1_p21), .INR(control_unit_1_p22), .CLR(control_unit_1_p23), .CP(CP_out), .A(TR_a));  // open: C
  Bit8_Register OUTR (.CLR(Reset_out), .CP(CP_out), .A(OUTR_a));  // open: I, Load, INR, C
  Hex_Digit_Display hex_digit_display_2 (.value(ram_1_dout[15:12]));  // open: dp
  Hex_Digit_Display hex_digit_display_3 (.value(ram_1_dout[11:8]));  // open: dp
  Hex_Digit_Display hex_digit_display_4 (.value(AR_a[11:8]));  // open: dp
  Hex_Digit_Display hex_digit_display_5 (.value(AR_a[7:4]));  // open: dp
  Hex_Digit_Display hex_digit_display_6 (.value(PC_a[11:8]));  // open: dp
  Hex_Digit_Display hex_digit_display_7 (.value(PC_a[7:4]));  // open: dp
  Hex_Digit_Display hex_digit_display_8 (.value(DR_a_4));  // open: dp
  Hex_Digit_Display hex_digit_display_9 (.value(DR_a_3));  // open: dp
  Hex_Digit_Display hex_digit_display_10 (.value(AC_a_4));  // open: dp
  Hex_Digit_Display hex_digit_display_11 (.value(AC_a_3));  // open: dp
  Hex_Digit_Display hex_digit_display_12 (.value(INPR_a[7:4]));  // open: dp
  Hex_Digit_Display hex_digit_display_13 (.value(INPR_a[3:0]));  // open: dp
  Hex_Digit_Display hex_digit_display_14 (.value(control_unit_1_p1_4));  // open: dp
  Hex_Digit_Display hex_digit_display_15 (.value(control_unit_1_p1_3));  // open: dp
  Hex_Digit_Display hex_digit_display_16 (.value(TR_a[15:12]));  // open: dp
  Hex_Digit_Display hex_digit_display_17 (.value(TR_a[11:8]));  // open: dp
  Hex_Digit_Display hex_digit_display_18 (.value(OUTR_a[7:4]));  // open: dp
  Hex_Digit_Display hex_digit_display_19 (.value(OUTR_a[3:0]));  // open: dp
  Hex_Digit_Display hex_digit_display_20 (.value(ram_1_dout[7:4]));  // open: dp
  Hex_Digit_Display hex_digit_display_21 (.value(ram_1_dout[3:0]));  // open: dp
  Hex_Digit_Display hex_digit_display_22 (.value(AR_a[3:0]));  // open: dp
  Hex_Digit_Display hex_digit_display_23 (.value(PC_a[3:0]));  // open: dp
  Hex_Digit_Display hex_digit_display_24 (.value(DR_a_2));  // open: dp
  Hex_Digit_Display hex_digit_display_25 (.value(DR_a));  // open: dp
  Hex_Digit_Display hex_digit_display_26 (.value(AC_a_2));  // open: dp
  Hex_Digit_Display hex_digit_display_27 (.value(AC_a));  // open: dp
  Hex_Digit_Display hex_digit_display_28 (.value(control_unit_1_p1_2));  // open: dp
  Hex_Digit_Display hex_digit_display_29 (.value(control_unit_1_p1));  // open: dp
  Hex_Digit_Display hex_digit_display_30 (.value(TR_a[7:4]));  // open: dp
  Hex_Digit_Display hex_digit_display_31 (.value(TR_a[3:0]));  // open: dp
  assign {controlled_buffer_1_out_3, controlled_buffer_1_out_2, controlled_buffer_1_out} = control_unit_1_p24 ? AR_a : 12'bz;  // Controlled_Buffer controlled_buffer_1
  assign {controlled_buffer_1_out_3, controlled_buffer_1_out_2, controlled_buffer_1_out} = control_unit_1_p25 ? PC_a : 12'bz;  // Controlled_Buffer controlled_buffer_2
  assign {controlled_buffer_3_out, controlled_buffer_1_out_3, controlled_buffer_1_out_2, controlled_buffer_1_out} = control_unit_1_p26 ? {DR_a_4, DR_a_3, DR_a_2, DR_a} : 16'bz;  // Controlled_Buffer controlled_buffer_3
  Hex_Digit_Display hex_digit_display_32 (.value(controlled_buffer_3_out));  // open: dp
  assign {controlled_buffer_3_out, controlled_buffer_1_out_3, controlled_buffer_1_out_2, controlled_buffer_1_out} = control_unit_1_p27 ? {AC_a_4, AC_a_3, AC_a_2, AC_a} : 16'bz;  // Controlled_Buffer controlled_buffer_4
  Hex_Digit_Display hex_digit_display_33 (.value(controlled_buffer_1_out_3));  // open: dp
  Hex_Digit_Display hex_digit_display_34 (.value(controlled_buffer_1_out_2));  // open: dp
  assign {controlled_buffer_3_out, controlled_buffer_1_out_3, controlled_buffer_1_out_2, controlled_buffer_1_out} = control_unit_1_p28 ? {control_unit_1_p1_4, control_unit_1_p1_3, control_unit_1_p1_2, control_unit_1_p1} : 16'bz;  // Controlled_Buffer controlled_buffer_5
  assign {controlled_buffer_3_out, controlled_buffer_1_out_3, controlled_buffer_1_out_2, controlled_buffer_1_out} = control_unit_1_p30 ? ram_1_dout : 16'bz;  // Controlled_Buffer controlled_buffer_6
  Hex_Digit_Display hex_digit_display_35 (.value(controlled_buffer_1_out));  // open: dp
  assign {controlled_buffer_3_out, controlled_buffer_1_out_3, controlled_buffer_1_out_2, controlled_buffer_1_out} = control_unit_1_p29 ? TR_a : 16'bz;  // Controlled_Buffer controlled_buffer_7
endmodule
